# Fritzing sketch Wiring diagram (saved by Fritzing 0.9.3b)
breadboards: 1

parts:
  MCU1 = Raspberry Pi Zero
  LED1 = RGB LED (com. cathode, rgb) [package="5 mm [THT]"]
  C1 = Electrolytic Capacitor [capacitance=100µF package="200 mil [THT, electrolytic]"]
  JACK1 = 2.1mm Barrel Jack with Terminal Block
  D1 = Diode [package=diode-1n4001]
  LED2 = RGB LED (com. cathode, rgb) [package="5 mm [THT]"]
  LED3 = RGB LED (com. cathode, rgb) [package="5 mm [THT]"]
  C2 = Capacitor [package=cap-pth-small2]
  S1 = Momentary Switch [package=ksa_sealed_tac_switch]

nets:
  N1: MCU1.pin_6, MCU1.pin_9, MCU1.pin_14, MCU1.pin_39, LED1.common_cathode, C1.-, JACK1.NEG, LED2.common_cathode, LED3.common_cathode, C2.1, S1.3, S1.4
  N2: MCU1.pin_12, LED1.red_anode
  N3: MCU1.pin_16, S1.1, S1.2
  N4: LED1.green_anode, LED2.green_anode, LED3.green_anode, C2.2
  N5: LED1.blue_anode, LED2.red_anode
  N6: C1.+, JACK1.POS, D1.C
  N7: LED2.blue_anode, LED3.red_anode
